# Fritzing sketch behemoth (saved by Fritzing 0.9.2b)
breadboards: 1

parts:
  Part1 = Arduino Uno (Rev3)
  Part2 = Bluetooth HC-06  # not connected
  uln2003a_stepper_motor_driver = Header 6 [package=molex-1x6_lock]
  LED1 = LED - 5mm [color="Red (633nm)" package="5 mm [THT]"]

nets:
  N1: Part1.D8, uln2003a_stepper_motor_driver.1
  N2: Part1.D9_PWM, uln2003a_stepper_motor_driver.2
  N3: Part1.D10_PWM/SS, uln2003a_stepper_motor_driver.3
  N4: Part1.D11_PWM/MOSI, uln2003a_stepper_motor_driver.4
  N5: Part1.D13/SCK, LED1.anode
  N6: Part1.GND, uln2003a_stepper_motor_driver.6, LED1.cathode
  N7: Part1.5V, uln2003a_stepper_motor_driver.5
